# Fritzing sketch IoTBox_Perfboard (saved by Fritzing 0.9.3b)
perfboards: 1

parts:
  S1 = SPST Switch [package=r_sw_th]
  LCD = Header 4 [package=jst-4-pth]
  Buzzer = Header 4 [package=jst-4-pth]
  Switch = Header 4 [package=jst-4-pth]
  J4 = Power Jack [package=power_jack_pth]
  L1 = Solenoid
  D1 = Diode [package=diode-1n4001]  # not connected
  Part1 = Photon  # not connected
  IC1 = MCP23017 I2C I/O Expander  # not connected
  J13 = Camdenboss CTB0158-2 [part_number=CTB0158-2 package=THT]
  J14 = Camdenboss CTB0158-2 [part_number=CTB0158-2 package=THT]

nets:
  N1: S1.O, J4.PWR
  N2: S1.P, J13.pin1
  N3: LCD.3, LCD.4
  N4: Buzzer.3, Buzzer.4
  N5: Switch.3, Switch.4
  N6: J4.GND, J13.pin2
  N7: L1.pin2, J14.pin1

custom parts:
  MCP23017 I2C I/O Expander: The MCP23017 uses two i2c pins (these can be shared with other i2c devices), and in exchange gives you 16 general purpose pins. You can set each of 16 pins to be input, output, input with a pullup or open drain. There's even the ability to get an interrupt via an external pin when any of the inputs change so you don't have to keep polling the chip.
